// Logisim project Demo CPU Restored.circ as structural Verilog: 17 circuits, main circuit CPUCore
module CPUCore (
);

  wire button_1_out, button_2_out, clearram_1_clockout, clearram_1_resetout, clock_1_out,
       controlunit_1_acc_we, controlunit_1_adr_addr, controlunit_1_adr_wh, controlunit_1_adr_wl,
       controlunit_1_alu_en, controlunit_1_flags_we, controlunit_1_gpr_re, controlunit_1_gpr_we,
       controlunit_1_ir_we, controlunit_1_out_re, controlunit_1_out_we, controlunit_1_pc_ld,
       controlunit_1_pc_rh, controlunit_1_pc_rl, controlunit_1_pc_we, controlunit_1_ram_re,
       controlunit_1_ram_we, controlunit_1_sp_addr, controlunit_1_sp_dec, controlunit_1_sp_inc,
       dipswitch_1_sw1, dipswitch_1_sw2, or_1_out, or_2_out, ramgate_1_clockout, ramgate_1_loadout,
       ramgate_1_storeout;
  wire [1:0] arithmaticlogicunit_1_flagsout, flags_1_flagsoutalu, flags_1_flagsoutcu;
  wire [2:0] controlunit_1_regselect;
  wire [3:0] controlunit_1_aluoperation;
  wire [7:0] accumulator_1_dataout, arithmaticlogicunit_1_output, clearram_1_dataout,
       gpr_block_1_stack_pointer_out, instructionreg_1_instructionout, programcounter_1_addressout,
       programcounter_1_addressout_2;
  wire [15:0] address_1_addressout, clearram_1_addrout, multiplexer_1_out, multiplexer_2_out,
       ramgate_1_addrout;

  Button button_1 (.out(button_1_out));
  or or_1 (or_1_out, button_1_out, dipswitch_1_sw1);
  Button button_2 (.out(button_2_out));
  DipSwitch #(.number(2)) dipswitch_1 (.sw1(dipswitch_1_sw1), .sw2(dipswitch_1_sw2));
  ClearRAM clearram_1 (
    .ResetIn(or_1_out), .ResetOut(clearram_1_resetout), .DataOut(clearram_1_dataout),
    .AddrOut(clearram_1_addrout), .ClockOut(clearram_1_clockout));
  or or_2 (or_2_out, clearram_1_resetout, button_2_out, dipswitch_1_sw2);
  Accumulator accumulator_1 (
    .DataOut(accumulator_1_dataout), .DataIn(clearram_1_dataout), .WE(controlunit_1_acc_we),
    .CLK(clock_1_out), .Reset(or_2_out));
  Output output_1 (
    .DataOut(clearram_1_dataout), .DataIn(arithmaticlogicunit_1_output), .WE(controlunit_1_out_we),
    .CLK(clock_1_out), .Reset(or_2_out), .RE(controlunit_1_out_re));
  ArithmaticLogicUnit arithmaticlogicunit_1 (
    .Output(arithmaticlogicunit_1_output), .FlagsOut(arithmaticlogicunit_1_flagsout),
    .InputA(clearram_1_dataout), .InputB(accumulator_1_dataout), .EN(controlunit_1_alu_en),
    .Operation(controlunit_1_aluoperation), .FlagsIn(flags_1_flagsoutalu));
  Flags flags_1 (
    .FlagsOutALU(flags_1_flagsoutalu), .FlagsOutCU(flags_1_flagsoutcu),
    .FlagsIn(arithmaticlogicunit_1_flagsout), .WE(controlunit_1_flags_we), .CLK(clock_1_out), .Reset(or_2_out));
  Clock clock_1 (.out(clock_1_out));
  InstructionReg instructionreg_1 (
    .InstructionOut(instructionreg_1_instructionout), .InstructionIn(clearram_1_dataout),
    .WE(controlunit_1_ir_we), .CLK(clock_1_out), .Reset(or_2_out));
  Address address_1 (
    .AddressOut(address_1_addressout), .Data_In(clearram_1_dataout), .WEL(controlunit_1_adr_wl),
    .WEH(controlunit_1_adr_wh), .CLK(clock_1_out), .Reset(or_2_out));
  assign clearram_1_dataout = controlunit_1_pc_rl ? programcounter_1_addressout_2 : 8'bz;  // Controlled_Buffer controlled_buffer_1
  ControlUnit controlunit_1 (
    .RegSelect(controlunit_1_regselect), .RAM_RE(controlunit_1_ram_re), .PC_WE(controlunit_1_pc_we),
    .GPR_RE(controlunit_1_gpr_re), .GPR_WE(controlunit_1_gpr_we), .SP_INC(controlunit_1_sp_inc),
    .SP_DEC(controlunit_1_sp_dec), .SP_ADDR(controlunit_1_sp_addr), .PC_RL(controlunit_1_pc_rl),
    .PC_RH(controlunit_1_pc_rh), .PC_LD(controlunit_1_pc_ld), .ADR_WL(controlunit_1_adr_wl),
    .ADR_WH(controlunit_1_adr_wh), .ADR_ADDR(controlunit_1_adr_addr), .RAM_WE(controlunit_1_ram_we),
    .ACC_WE(controlunit_1_acc_we), .FLAGS_WE(controlunit_1_flags_we), .OUT_RE(controlunit_1_out_re),
    .OUT_WE(controlunit_1_out_we), .ALUOperation(controlunit_1_aluoperation), .ALU_EN(controlunit_1_alu_en),
    .IR_WE(controlunit_1_ir_we), .Instruction(instructionreg_1_instructionout), .Flags(flags_1_flagsoutcu),
    .Reset(or_2_out), .CLK(clock_1_out));
  ProgramCounter programcounter_1 (
    .AddressOut({programcounter_1_addressout_2, programcounter_1_addressout}), .CLK(clock_1_out),
    .AddressIn(address_1_addressout), .LD(controlunit_1_pc_ld), .WE(controlunit_1_pc_we), .Reset(or_2_out));
  assign clearram_1_dataout = controlunit_1_pc_rh ? programcounter_1_addressout : 8'bz;  // Controlled_Buffer controlled_buffer_2
  Multiplexer #(.enable("false"), .width(16)) multiplexer_1 (
    .in0({programcounter_1_addressout_2, programcounter_1_addressout}), .in1(address_1_addressout),
    .out(multiplexer_1_out), .sel(controlunit_1_adr_addr));
  Multiplexer #(.enable("false"), .width(16)) multiplexer_2 (
    .in0(multiplexer_1_out), .in1({8'h1, gpr_block_1_stack_pointer_out}), .out(multiplexer_2_out),
    .sel(controlunit_1_sp_addr));
  RAMGate ramgate_1 (
    .AddrOut(ramgate_1_addrout), .LoadOut(ramgate_1_loadout), .StoreOut(ramgate_1_storeout),
    .ClockOut(ramgate_1_clockout), .AddrIn(multiplexer_2_out), .ClearAddr(clearram_1_addrout),
    .LoadIn(controlunit_1_ram_re), .StoreIn(controlunit_1_ram_we), .ClockIn(clock_1_out),
    .ClearClock(clearram_1_clockout), .ClearEnable(clearram_1_resetout));
  RAM #(.addrWidth(16), .databus("bidir")) Main_RAM (
    .addr(ramgate_1_addrout), .data(clearram_1_dataout));  // open: we, oe, clk
  GPR_Block gpr_block_1 (
    .Data_Out(clearram_1_dataout), .Stack_Pointer_Out(gpr_block_1_stack_pointer_out),
    .IncSP(controlunit_1_sp_inc), .DecSP(controlunit_1_sp_dec), .Write_Enable(controlunit_1_gpr_we),
    .Data_In(clearram_1_dataout), .Register_Select(controlunit_1_regselect), .Clock(clock_1_out),
    .Clear(or_2_out), .Read_Enable(controlunit_1_gpr_re));

  // Notes on the sheet:
  //   Clear RAM
  //   Reset CPU
endmodule

// Control Unit
module ControlUnit (
  input  CLK,
  input  Reset,
  input  [1:0] Flags,
  input  [7:0] Instruction,
  output IR_WE,
  output RAM_RE,
  output PC_WE,
  output GPR_RE,
  output GPR_WE,
  output SP_INC,
  output SP_DEC,
  output SP_ADDR,
  output PC_RL,
  output PC_RH,
  output PC_LD,
  output ADR_WL,
  output ADR_WH,
  output ADR_ADDR,
  output RAM_WE,
  output ACC_WE,
  output FLAGS_WE,
  output OUT_RE,
  output OUT_WE,
  output [3:0] ALUOperation,
  output [2:0] RegSelect,
  output ALU_EN
);

  wire and_2_out, comparator_3_lt, comparator_4_eq, comparator_5_eq, nor_1_out, not_1_out, or_1_out,
       or_2_out, priority_encoder_1_p4, priority_encoder_1_p5, priority_encoder_1_p6, priority_encoder_1_p7,
       stepper_1_setep2low, stepper_1_setep3low, stepper_1_step0high, stepper_1_step1high,
       stepper_1_step1low, stepper_1_step2high, stepper_1_step3high;
  wire [1:0] and_1_out, bit_extender_2_out, priority_encoder_1_p3;
  wire [2:0] bitfinder_1_index;
  wire [31:0] All_Other_Instructions_data, and_3_out, and_4_out, and_5_out, and_6_out, bit_extender_1_out,
       bit_extender_3_out, bit_extender_4_out, bit_extender_5_out, bit_extender_6_out, bit_extender_7_out,
       Conditional_Jump_data, Extra_No_Operand_Instructions_data, No_Operand_Instructions_data;
  wire [31:8] or_6_out;

  BitFinder #(.\type ("high1")) bitfinder_1 (.in(Instruction), .index(bitfinder_1_index));  // open: found
  Comparator #(.mode("unsigned"), .width(3)) comparator_1 (.a(bitfinder_1_index), .b(3'b100));  // open: gt, eq, lt
  Comparator #(.mode("unsigned"), .width(3)) comparator_2 ();  // open: a, b, gt, eq, lt
  not not_1 (not_1_out, Instruction[7]);
  or or_1 (or_1_out, or_6_out[23], Reset);
  Stepper stepper_1 (
    .Step3High(stepper_1_step3high), .Step0Low(IR_WE), .Step0High(stepper_1_step0high),
    .Step1Low(stepper_1_step1low), .Step1High(stepper_1_step1high), .Setep2Low(stepper_1_setep2low),
    .Step2High(stepper_1_step2high), .Setep3Low(stepper_1_setep3low), .Reset(or_1_out), .CLK(CLK));  // open: Setep4Low, Step4High
  or or_2 (or_2_out, stepper_1_step1low, stepper_1_step1high);
  // Priority_Encoder #(.select(2)) priority_encoder_1: pin names not known; wires that end beside it: stepper_1_step0high, or_2_out, priority_encoder_1_p3, priority_encoder_1_p4, priority_encoder_1_p5, priority_encoder_1_p6, priority_encoder_1_p7
  assign and_1_out = priority_encoder_1_p3 & bit_extender_2_out;  // AND_Gate and_1, 2 bits wide
  assign bit_extender_1_out = {{31{not_1_out}}, not_1_out};  // Bit_Extender bit_extender_1
  or or_3 (priority_encoder_1_p4, stepper_1_setep2low, stepper_1_step2high);
  or or_4 (priority_encoder_1_p6, stepper_1_setep3low, stepper_1_step3high);
  or or_5 (priority_encoder_1_p7, stepper_1_step0high, or_2_out, priority_encoder_1_p4, priority_encoder_1_p6);
  and and_2 (and_2_out, priority_encoder_1_p5, priority_encoder_1_p7);
  assign bit_extender_2_out = {{1{and_2_out}}, and_2_out};  // Bit_Extender bit_extender_2
  ROM #(.addrWidth(6), .dataWidth(32)) No_Operand_Instructions (
    .addr({Instruction[2:0], and_1_out, CLK}), .data(No_Operand_Instructions_data));
  ROM #(.dataWidth(32)) Conditional_Jump (
    .addr({Instruction[2:0], Flags, and_1_out, CLK}), .data(Conditional_Jump_data));
  ROM #(.addrWidth(6), .dataWidth(32)) Extra_No_Operand_Instructions (
    .addr({Instruction[2:0], and_1_out, CLK}), .data(Extra_No_Operand_Instructions_data));
  ROM #(.dataWidth(32)) All_Other_Instructions (
    .addr({Instruction[7:3], and_1_out, CLK}), .data(All_Other_Instructions_data));
  assign bit_extender_3_out = {{31{and_2_out}}, and_2_out};  // Bit_Extender bit_extender_3
  assign bit_extender_4_out = {{31{comparator_3_lt}}, comparator_3_lt};  // Bit_Extender bit_extender_4
  Comparator #(.mode("unsigned"), .width(3)) comparator_3 (
    .a(bitfinder_1_index), .b(3'b011), .lt(comparator_3_lt));  // open: gt, eq
  assign bit_extender_5_out = {{31{comparator_4_eq}}, comparator_4_eq};  // Bit_Extender bit_extender_5
  Comparator #(.mode("unsigned"), .width(4)) comparator_4 (
    .a(Instruction[6:3]), .b(4'b0110), .eq(comparator_4_eq));  // open: gt, lt
  assign bit_extender_6_out = {{31{comparator_5_eq}}, comparator_5_eq};  // Bit_Extender bit_extender_6
  Comparator #(.mode("unsigned"), .width(4)) comparator_5 (
    .a(Instruction[6:3]), .b(4'b1101), .eq(comparator_5_eq));  // open: gt, lt
  assign bit_extender_7_out = {{31{nor_1_out}}, nor_1_out};  // Bit_Extender bit_extender_7
  nor nor_1 (nor_1_out, comparator_5_eq, comparator_4_eq, comparator_3_lt);
  assign and_3_out = bit_extender_3_out & No_Operand_Instructions_data & bit_extender_4_out & bit_extender_1_out;  // AND_Gate and_3, 32 bits wide
  assign and_4_out = bit_extender_3_out & Conditional_Jump_data & bit_extender_5_out & bit_extender_1_out;  // AND_Gate and_4, 32 bits wide
  assign and_5_out = bit_extender_3_out & Extra_No_Operand_Instructions_data & bit_extender_6_out & bit_extender_1_out;  // AND_Gate and_5, 32 bits wide
  assign and_6_out = bit_extender_3_out & All_Other_Instructions_data & bit_extender_7_out & bit_extender_1_out;  // AND_Gate and_6, 32 bits wide
  assign {or_6_out[31:19], OUT_WE, OUT_RE, or_6_out[16], FLAGS_WE, ACC_WE, RAM_WE, or_6_out[12], ADR_ADDR, ADR_WH, ADR_WL, or_6_out[8], PC_LD, PC_RH, PC_RL, SP_ADDR, SP_DEC, SP_INC, GPR_WE, GPR_RE} = and_3_out | and_4_out | and_5_out | and_6_out;  // OR_Gate or_6, 32 bits wide
  or or_7 (RAM_RE, IR_WE, or_6_out[12]);
  or or_8 (PC_WE, IR_WE, or_6_out[8]);

  assign ALU_EN = Instruction[7];
  assign ALUOperation = Instruction[6:3];
  assign RegSelect = Instruction[2:0];
endmodule

// Arithmatic Logic Unit
module ArithmaticLogicUnit (
  input  [7:0] InputA,
  input  [7:0] InputB,
  input  [1:0] FlagsIn,
  input  EN,
  input  [3:0] Operation,
  output [7:0] Output,
  output [1:0] FlagsOut
);

  wire adder_1_cout, adder_2_cout, and_2_out, comparator_1_eq, subtractor_1_bout, subtractor_2_bout;
  wire [2:0] bit_extender_1_out;
  wire [7:0] adder_1_out, adder_2_out, and_1_out, nand_1_out, negator_1_out, nor_1_out, not_1_out, or_1_out,
       shifter_1_out, shifter_2_out, subtractor_1_out, subtractor_2_out, xor_1_out;

  Adder adder_1 (.a(InputA), .b(InputB), .out(adder_1_out), .cin(and_2_out), .cout(adder_1_cout));
  Subtractor subtractor_1 (.a(InputA), .b(InputB), .out(subtractor_1_out), .bout(subtractor_1_bout));  // open: bin
  Negator negator_1 (.in(InputA), .out(negator_1_out));
  Adder adder_2 (.a(InputA), .b(8'h1), .out(adder_2_out), .cout(adder_2_cout));  // open: cin
  Subtractor subtractor_2 (.a(InputA), .b(8'h1), .out(subtractor_2_out), .bout(subtractor_2_bout));  // open: bin
  assign and_1_out = InputA & InputB;  // AND_Gate and_1, 8 bits wide
  assign nand_1_out = ~(InputA & InputB);  // NAND_Gate nand_1, 8 bits wide
  assign or_1_out = InputA | InputB;  // OR_Gate or_1, 8 bits wide
  assign nor_1_out = ~(InputA | InputB);  // NOR_Gate nor_1, 8 bits wide
  assign not_1_out = ~InputA;  // NOT_Gate not_1, 8 bits wide
  assign xor_1_out = InputA ^ InputB;  // XOR_Gate xor_1, 8 bits wide
  Bit_Extender #(.out_width(3)) bit_extender_1 (.in(InputB), .out(bit_extender_1_out));
  Shifter #(.shift("lr")) shifter_1 (.in(InputA), .\dist (bit_extender_1_out), .out(shifter_1_out));
  Shifter shifter_2 (.in(InputA), .\dist (bit_extender_1_out), .out(shifter_2_out));
  Multiplexer #(.select(4), .width(8)) multiplexer_1 (
    .in0(adder_1_out), .in1(adder_1_out), .in2(subtractor_1_out), .in3(negator_1_out), .in4(adder_2_out),
    .in5(subtractor_2_out), .in6(and_1_out), .in7(and_1_out), .in8(nand_1_out), .in9(or_1_out),
    .in10(nor_1_out), .in11(not_1_out), .in12(xor_1_out), .in13(shifter_1_out), .in14(shifter_2_out),
    .in15(subtractor_1_out), .out(Output), .sel(Operation), .en(EN));
  Multiplexer #(.select(4)) multiplexer_2 (
    .in0(adder_1_cout), .in1(adder_1_cout), .in2(subtractor_1_bout), .in3(1'b0), .in4(adder_2_cout),
    .in5(subtractor_2_bout), .in6(1'b0), .in7(1'b0), .in8(1'b0), .in9(1'b0), .in10(1'b0), .in11(1'b0),
    .in12(1'b0), .in13(1'b0), .in14(1'b0), .in15(subtractor_1_bout), .out(FlagsOut[1]), .sel(Operation),
    .en(EN));
  and and_2 (and_2_out, FlagsIn[1], comparator_1_eq);
  Comparator #(.mode("unsigned"), .width(4)) comparator_1 (
    .a(Operation), .b(4'b0000), .eq(comparator_1_eq));  // open: gt, lt
  Comparator #(.mode("unsigned")) comparator_2 (.a(Output), .b({8{1'b0}}), .eq(FlagsOut[0]));  // open: gt, lt
endmodule

module Address (
  input  [7:0] Data_In,
  input  WEL,
  input  WEH,
  input  CLK,
  input  Reset,
  output [15:0] AddressOut
);

  Register #(.trigger("falling")) TempLow (.D(Data_In), .en(WEL), .clk(CLK), .Q(AddressOut[7:0]), .clr(Reset));
  Register TempHigh (.D(Data_In), .en(WEH), .clk(CLK), .Q(AddressOut[15:8]), .clr(Reset));
endmodule

module Accumulator (
  input  [7:0] DataIn,
  input  WE,
  input  CLK,
  input  Reset,
  output [7:0] DataOut
);

  Register #(.trigger("falling")) Accumulator (.D(DataIn), .en(WE), .clk(CLK), .Q(DataOut), .clr(Reset));
endmodule

module Output (
  input  [7:0] DataIn,
  input  WE,
  input  CLK,
  input  Reset,
  input  RE,
  output [7:0] DataOut
);

  wire [7:0] Output_q;

  Register #(.trigger("falling")) Output (.D(DataIn), .en(WE), .clk(CLK), .Q(Output_q), .clr(Reset));
  assign DataOut = RE ? Output_q : 8'bz;  // Controlled_Buffer controlled_buffer_1
endmodule

module Flags (
  input  [1:0] FlagsIn,
  input  WE,
  input  CLK,
  input  Reset,
  output [1:0] FlagsOutALU,
  output [1:0] FlagsOutCU
);

  Register #(.trigger("falling"), .width(2)) Flags (.D(FlagsIn), .en(WE), .clk(CLK), .Q(FlagsOutALU), .clr(Reset));

  assign FlagsOutCU = FlagsOutALU;
endmodule

// PC
module ProgramCounter (
  input  [15:0] AddressIn,
  input  LD,
  input  WE,
  input  Reset,
  input  CLK,
  output [15:0] AddressOut
);

  wire dualedgegenerator_1_triggerout;
  wire [15:0] adder_1_out, multiplexer_1_out;

  Register #(.width(16)) ProgramCounter (
    .D(multiplexer_1_out), .en(WE), .clk(dualedgegenerator_1_triggerout), .Q(AddressOut), .clr(Reset));
  Adder #(.width(16)) adder_1 (.a(AddressOut), .b({16{1'b0}}), .out(adder_1_out), .cin(1'b1));  // open: cout
  Multiplexer #(.enable("false"), .width(16)) multiplexer_1 (
    .in0(adder_1_out), .in1(AddressIn), .out(multiplexer_1_out), .sel(LD));
  DualEdgeGenerator dualedgegenerator_1 (.CLKin(CLK), .TriggerOut(dualedgegenerator_1_triggerout));
endmodule

// Instruction
module InstructionReg (
  input  [7:0] InstructionIn,
  input  WE,
  input  CLK,
  input  Reset,
  output [7:0] InstructionOut
);

  Register Instruction (.D(InstructionIn), .en(WE), .clk(CLK), .Q(InstructionOut), .clr(Reset));
endmodule

module Stepper (
  input  Reset,
  input  CLK,
  output Step0Low,
  output Step0High,
  output Step1Low,
  output Step1High,
  output Setep2Low,
  output Step2High,
  output Setep3Low,
  output Step3High,
  output Setep4Low,
  output Step4High
);

  wire not_1_out, or_1_out, or_2_out, or_3_out, or_4_out, or_5_out, or_6_out, or_7_out, or_8_out, or_9_out,
       Step_0_High_q, Step_0_Low_q, Step_1_High_q, Step_1_Low_q, Step_2_High_q, Step_2_Low_q, Step_3_High_q,
       Step_3_Low_q, Step_4_High_q, Step_4_Low_q;

  S_R_Flip_Flop #(.trigger("falling")) Step_0_Low (
    .S(Step_4_High_q), .R(1'b0), .clk(CLK), .Q(Step_0_Low_q), .reset(Step_0_High_q), .preset(Reset));  // open: Qn
  not not_1 (not_1_out, Reset);
  and and_1 (Step0Low, Step_0_Low_q, not_1_out, ~Step_0_High_q);  // AND_Gate
  S_R_Flip_Flop Step_0_High (
    .S(Step_0_Low_q), .R(1'b0), .clk(CLK), .Q(Step_0_High_q), .reset(or_1_out));  // open: Qn, preset
  or or_1 (or_1_out, Reset, Step_1_Low_q);
  S_R_Flip_Flop #(.trigger("falling")) Step_1_Low (
    .S(Step_0_High_q), .R(1'b0), .clk(CLK), .Q(Step_1_Low_q), .reset(or_2_out));  // open: Qn, preset
  or or_2 (or_2_out, Reset, Step_1_High_q);
  and and_2 (Step0High, Step_0_High_q, not_1_out, ~Step_1_Low_q);  // AND_Gate
  S_R_Flip_Flop Step_1_High (
    .S(Step_1_Low_q), .R(1'b0), .clk(CLK), .Q(Step_1_High_q), .reset(or_3_out));  // open: Qn, preset
  or or_3 (or_3_out, Reset, Step_2_Low_q);
  and and_3 (Step1Low, Step_1_Low_q, not_1_out, ~Step_1_High_q);  // AND_Gate
  S_R_Flip_Flop #(.trigger("falling")) Step_2_Low (
    .S(Step_1_High_q), .R(1'b0), .clk(CLK), .Q(Step_2_Low_q), .reset(or_4_out));  // open: Qn, preset
  or or_4 (or_4_out, Reset, Step_2_High_q);
  and and_4 (Step1High, Step_1_High_q, not_1_out, ~Step_2_Low_q);  // AND_Gate
  S_R_Flip_Flop Step_2_High (
    .S(Step_2_Low_q), .R(1'b0), .clk(CLK), .Q(Step_2_High_q), .reset(or_5_out));  // open: Qn, preset
  or or_5 (or_5_out, Reset, Step_3_Low_q);
  and and_5 (Setep2Low, Step_2_Low_q, not_1_out, ~Step_2_High_q);  // AND_Gate
  S_R_Flip_Flop #(.trigger("falling")) Step_3_Low (
    .S(Step_2_High_q), .R(1'b0), .clk(CLK), .Q(Step_3_Low_q), .reset(or_6_out));  // open: Qn, preset
  and and_6 (Step2High, Step_2_High_q, not_1_out, ~Step_3_Low_q);  // AND_Gate
  S_R_Flip_Flop Step_3_High (
    .S(Step_3_Low_q), .R(1'b0), .clk(CLK), .Q(Step_3_High_q), .reset(or_7_out));  // open: Qn, preset
  or or_6 (or_6_out, Reset, Step_3_High_q);
  and and_7 (Setep3Low, Step_3_Low_q, not_1_out, ~Step_3_High_q);  // AND_Gate
  or or_7 (or_7_out, Reset, Step_4_Low_q);
  and and_8 (Step3High, Step_3_High_q, not_1_out, ~Step_4_Low_q);  // AND_Gate
  S_R_Flip_Flop #(.trigger("falling")) Step_4_Low (
    .S(Step_3_High_q), .R(1'b0), .clk(CLK), .Q(Step_4_Low_q), .reset(or_8_out));  // open: Qn, preset
  or or_8 (or_8_out, Reset, Step_4_High_q);
  and and_9 (Setep4Low, Step_4_Low_q, not_1_out, ~Step_4_High_q);  // AND_Gate
  S_R_Flip_Flop Step_4_High (
    .S(Step_4_Low_q), .R(1'b0), .clk(CLK), .Q(Step_4_High_q), .reset(or_9_out));  // open: Qn, preset
  or or_9 (or_9_out, Reset, Step_0_Low_q);
  and and_10 (Step4High, Step_4_High_q, not_1_out, ~Step_0_Low_q);  // AND_Gate
endmodule

// Conditional Jump
module ConditionalJump (
  input  [1:0] Flags,
  input  Step1High,
  input  Step2Low,
  input  Step1Low,
  input  [2:0] Condition,
  input  Enable,
  output PC_Load,
  output PC_Set,
  output ResetStepper
);

  wire and_1_out, and_2_out, and_3_out, and_4_out, and_5_out, and_6_out, and_7_out, and_8_out, and_9_out,
       and_10_out, buffer_1_out, buffer_2_out, buffer_3_out, buffer_4_out, buffer_5_out, buffer_6_out,
       buffer_7_out, buffer_8_out, buffer_9_out, buffer_10_out, buffer_11_out, buffer_12_out, buffer_13_out,
       d_ff_1_q, decoder_1_out0, decoder_1_out1, decoder_1_out2, decoder_1_out3, decoder_1_out4,
       decoder_1_out5, not_1_out, not_2_out, or_1_out;

  not not_1 (not_1_out, Flags[1]);
  not not_2 (not_2_out, Flags[0]);
  Decoder #(.select(3)) decoder_1 (
    .out0(decoder_1_out0), .out1(decoder_1_out1), .out2(decoder_1_out2), .out3(decoder_1_out3),
    .out4(decoder_1_out4), .out5(decoder_1_out5), .sel(Condition), .en(Enable));  // open: out6, out7
  and and_1 (and_1_out, not_2_out, decoder_1_out0);
  and and_2 (and_2_out, Flags[0], decoder_1_out1);
  and and_3 (and_3_out, Flags[1], decoder_1_out2);
  and and_4 (and_4_out, not_1_out, decoder_1_out3);
  and and_5 (and_5_out, not_2_out, not_1_out, decoder_1_out4);
  and and_6 (and_6_out, Flags[0], not_1_out, decoder_1_out5);
  and and_7 (and_7_out, not_2_out, Flags[1], decoder_1_out5);
  and and_8 (and_8_out, Flags[0], Flags[1], decoder_1_out5);
  or or_1 (or_1_out, and_1_out, and_2_out, and_3_out, and_4_out, and_5_out, and_6_out, and_7_out, and_8_out);
  D_Flip_Flop d_ff_1 (.D(or_1_out), .clk(Step1Low), .Q(d_ff_1_q), .reset(buffer_1_out));  // open: Qn, preset
  and and_9 (and_9_out, Step1High, Enable, d_ff_1_q);
  and and_10 (and_10_out, Step2Low, Enable, d_ff_1_q);
  and and_11 (ResetStepper, Step2Low, Enable);
  buf buffer_1 (buffer_1_out, buffer_2_out);
  buf buffer_2 (buffer_2_out, buffer_3_out);
  buf buffer_3 (buffer_3_out, buffer_12_out);
  buf buffer_4 (buffer_4_out, and_9_out);
  buf buffer_5 (buffer_5_out, buffer_4_out);
  buf buffer_6 (buffer_6_out, buffer_5_out);
  buf buffer_7 (buffer_7_out, buffer_6_out);
  buf buffer_8 (buffer_8_out, and_10_out);
  buf buffer_9 (buffer_9_out, buffer_8_out);
  buf buffer_10 (buffer_10_out, buffer_9_out);
  buf buffer_11 (buffer_11_out, buffer_10_out);
  buf buffer_12 (buffer_12_out, buffer_13_out);
  buf buffer_13 (buffer_13_out, ResetStepper);
  buf buffer_14 (PC_Load, buffer_7_out);
  buf buffer_15 (PC_Set, buffer_11_out);
endmodule

module ClearGPR (
  input  ResetIn,
  output ResetOut,
  output [7:0] DataOut,
  output [2:0] AddrOut,
  output ClockOut
);

  wire counter_1_carry;
  wire [3:3] counter_1_q;

  Counter #(.max('hf), .width(4)) counter_1 (
    .clr(counter_1_q[3]), .count(ResetOut), .clk(ClockOut), .carry(counter_1_carry),
    .Q({counter_1_q[3], AddrOut}));  // open: load, up, D
  Clock clock_1 (.out(ClockOut));
  S_R_Flip_Flop #(.trigger("high")) s_r_ff_1 (
    .clk(counter_1_carry), .Q(ResetOut), .reset(counter_1_q[3]), .preset(ResetIn));  // open: S, R, Qn
  assign DataOut = ResetOut ? {8{1'b0}} : 8'bz;  // Controlled_Buffer controlled_buffer_1
endmodule

module GPRGate (
  input  ClearEnable,
  input  [2:0] AddrIn,
  input  [2:0] ClearAddr,
  input  LoadIn,
  input  StoreIn,
  input  ClockIn,
  input  ClearClock,
  output [2:0] AddrOut,
  output LoadOut,
  output StoreOut,
  output ClockOut
);

  Multiplexer #(.enable("false"), .width(3)) multiplexer_1 (
    .in0(AddrIn), .in1(ClearAddr), .out(AddrOut), .sel(ClearEnable));
  and and_1 (LoadOut, ~ClearEnable, LoadIn);  // AND_Gate
  Multiplexer #(.enable("false")) multiplexer_2 (.in0(StoreIn), .in1(ClearEnable), .out(StoreOut), .sel(ClearEnable));
  Multiplexer #(.enable("false")) multiplexer_3 (.in0(ClockIn), .in1(ClearClock), .out(ClockOut), .sel(ClearEnable));
endmodule

module RAMGate (
  input  ClearEnable,
  input  [15:0] AddrIn,
  input  [15:0] ClearAddr,
  input  LoadIn,
  input  StoreIn,
  input  ClockIn,
  input  ClearClock,
  output [15:0] AddrOut,
  output LoadOut,
  output StoreOut,
  output ClockOut
);

  Multiplexer #(.enable("false"), .width(16)) multiplexer_1 (
    .in0(AddrIn), .in1(ClearAddr), .out(AddrOut), .sel(ClearEnable));
  and and_1 (LoadOut, ~ClearEnable, LoadIn);  // AND_Gate
  Multiplexer #(.enable("false")) multiplexer_2 (.in0(StoreIn), .in1(ClearEnable), .out(StoreOut), .sel(ClearEnable));
  Multiplexer #(.enable("false")) multiplexer_3 (.in0(ClockIn), .in1(ClearClock), .out(ClockOut), .sel(ClearEnable));
endmodule

module ClearRAM (
  input  ResetIn,
  output ResetOut,
  output [7:0] DataOut,
  output [15:0] AddrOut,
  output ClockOut
);

  wire counter_1_carry;
  wire [16:16] counter_1_q;

  Counter #(.max('h1ffff), .width(17)) counter_1 (
    .clr(counter_1_q[16]), .count(ResetOut), .clk(ClockOut), .carry(counter_1_carry),
    .Q({counter_1_q[16], AddrOut}));  // open: load, up, D
  Clock clock_1 (.out(ClockOut));
  S_R_Flip_Flop #(.trigger("high")) s_r_ff_1 (
    .clk(counter_1_carry), .Q(ResetOut), .reset(counter_1_q[16]), .preset(ResetIn));  // open: S, R, Qn
  assign DataOut = ResetOut ? {8{1'b0}} : 8'bz;  // Controlled_Buffer controlled_buffer_1
endmodule

module GPR_Block (
  input  [7:0] Data_In,
  input  Write_Enable,
  input  [2:0] Register_Select,
  input  IncSP,
  input  DecSP,
  input  Clock,
  input  Clear,
  input  Read_Enable,
  output [7:0] Data_Out,
  output [7:0] Stack_Pointer_Out
);

  wire demultiplexer_1_out0, demultiplexer_1_out1, demultiplexer_1_out2, demultiplexer_1_out3,
       demultiplexer_1_out4, demultiplexer_1_out5, demultiplexer_1_out6, demultiplexer_1_out7, or_1_out,
       or_2_out;
  wire [7:0] adder_1_out, multiplexer_1_out, multiplexer_2_out, r0_q, r1_q, r2_q, r3_q, r4_q, r5_q, r6_q,
       subtractor_1_out;

  Adder adder_1 (.a(Stack_Pointer_Out), .b({8{1'b0}}), .out(adder_1_out), .cin(IncSP));  // open: cout
  Subtractor subtractor_1 (.a(Stack_Pointer_Out), .b({8{1'b0}}), .out(subtractor_1_out), .bin(DecSP));  // open: bout
  or or_1 (or_1_out, IncSP, DecSP);
  Multiplexer #(.enable("false"), .width(8)) multiplexer_1 (
    .in0(Data_In), .in1(multiplexer_2_out), .out(multiplexer_1_out), .sel(or_1_out));
  Multiplexer #(.enable("false"), .width(8)) multiplexer_2 (
    .in0(adder_1_out), .in1(subtractor_1_out), .out(multiplexer_2_out), .sel(DecSP));
  Demultiplexer #(.enable("false"), .select(3)) demultiplexer_1 (
    .out0(demultiplexer_1_out0), .out1(demultiplexer_1_out1), .out2(demultiplexer_1_out2),
    .out3(demultiplexer_1_out3), .out4(demultiplexer_1_out4), .out5(demultiplexer_1_out5),
    .out6(demultiplexer_1_out6), .out7(demultiplexer_1_out7), .in(Write_Enable), .sel(Register_Select));
  or or_2 (or_2_out, or_1_out, demultiplexer_1_out7);
  Register #(.trigger("falling")) r0 (.D(Data_In), .en(demultiplexer_1_out0), .clk(Clock), .Q(r0_q), .clr(Clear));
  Register #(.trigger("falling")) r1 (.D(Data_In), .en(demultiplexer_1_out1), .clk(Clock), .Q(r1_q), .clr(Clear));
  Register #(.trigger("falling")) r2 (.D(Data_In), .en(demultiplexer_1_out2), .clk(Clock), .Q(r2_q), .clr(Clear));
  Register #(.trigger("falling")) r3 (.D(Data_In), .en(demultiplexer_1_out3), .clk(Clock), .Q(r3_q), .clr(Clear));
  Register #(.trigger("falling")) r4 (.D(Data_In), .en(demultiplexer_1_out4), .clk(Clock), .Q(r4_q), .clr(Clear));
  Register #(.trigger("falling")) r5 (.D(Data_In), .en(demultiplexer_1_out5), .clk(Clock), .Q(r5_q), .clr(Clear));
  Register #(.trigger("falling")) r6 (.D(Data_In), .en(demultiplexer_1_out6), .clk(Clock), .Q(r6_q), .clr(Clear));
  Register #(.trigger("falling")) r7 (
    .D(multiplexer_1_out), .en(or_2_out), .clk(Clock), .Q(Stack_Pointer_Out), .clr(Clear));
  Multiplexer #(.disabled("Z"), .select(3), .width(8)) multiplexer_3 (
    .in0(r0_q), .in1(r1_q), .in2(r2_q), .in3(r3_q), .in4(r4_q), .in5(r5_q), .in6(r6_q),
    .in7(Stack_Pointer_Out), .out(Data_Out), .sel(Register_Select), .en(Read_Enable));

  // Other names for the same wires on the sheet: sp[7:0] = Stack_Pointer_Out; spIn[7:0] = Data_In
endmodule

module DualEdgeGenerator (
  input  CLKin,
  output TriggerOut
);

  wire buffer_1_out, buffer_2_out, buffer_3_out, buffer_4_out, buffer_5_out, buffer_6_out, buffer_7_out,
       buffer_8_out, buffer_9_out, buffer_10_out, buffer_11_out, buffer_12_out, xor_1_out, xor_2_out,
       xor_3_out, xor_4_out;

  xor xor_1 (xor_1_out, 1'b1, CLKin);
  xor xor_2 (xor_2_out, CLKin, 1'b0);
  buf buffer_1 (buffer_1_out, xor_1_out);
  buf buffer_2 (buffer_2_out, buffer_1_out);
  buf buffer_3 (buffer_3_out, xor_2_out);
  buf buffer_4 (buffer_4_out, buffer_3_out);
  buf buffer_5 (buffer_5_out, buffer_2_out);
  buf buffer_6 (buffer_6_out, buffer_5_out);
  buf buffer_7 (buffer_7_out, buffer_6_out);
  buf buffer_8 (buffer_8_out, buffer_7_out);
  buf buffer_9 (buffer_9_out, buffer_4_out);
  buf buffer_10 (buffer_10_out, buffer_9_out);
  buf buffer_11 (buffer_11_out, buffer_10_out);
  buf buffer_12 (buffer_12_out, buffer_11_out);
  xor xor_3 (xor_3_out, xor_1_out, buffer_8_out);
  or or_1 (TriggerOut, xor_3_out, xor_4_out);
  xor xor_4 (xor_4_out, buffer_12_out, xor_2_out);
endmodule
